# Fritzing sketch un-diodo-con-pulsador (saved by Fritzing 0.9.10b)
breadboards: 1

parts:
  Componente1 = Arduino Uno (Rev3)
  LED1 = LED - 3mm [color="Red (633nm)" current=0.030 package="3 mm [THT]"]
  S2 = Pushbutton [package="[SMD]"]

nets:
  N1: Componente1.D13/SCK, LED1.anode
  N2: Componente1.GND, LED1.cathode, S2.Pin_1, S2.Pin_2
  N3: Componente1.D2, S2.Pin_3, S2.Pin_4
