# Fritzing sketch un-diodo-sin-resistencia (saved by Fritzing 0.9.10b)
breadboards: 1

parts:
  Componente1 = Arduino Uno (Rev3)
  LED1 = LED - 3mm [color="Red (633nm)" current=0.030 package="3 mm [THT]"]

nets:
  N1: Componente1.D13/SCK, LED1.anode
  N2: Componente1.GND, LED1.cathode
