# Fritzing sketch un-pulsador-y-buzzer (saved by Fritzing 0.9.7b)
breadboards: 1

parts:
  Componente1 = Arduino Uno (Rev3)
  R1 = Resistor [tolerance=±5% resistance=470 package="1206 [SMD]"]
  LED1 = LED - 3mm [color="Red (633nm)" current=0.030 package="3 mm [THT]"]
  S2 = Pushbutton [package="[SMD]"]  # not connected

nets:
  N1: Componente1.D13/SCK, R1.Pin_0
  N2: Componente1.GND, LED1.cathode
